# Fritzing sketch gordonnet_tempmon (saved by Fritzing 0.9.3b)
breadboards: 1

parts:
  LCD_1602 = I2C LCD1602
  R1 = Resistor [tolerance=±5% resistance=10k package=THT]
  DHT11 = DHT11 Humiture Sensor
  S1 = Reed switch [package=THT]
  T-Cobbler = T-Cobbler
  RBG = Dule-Color LED
  Active_Buzzer = Buzzer 12mm [package=buzzer-ccv-kit]  # not connected

nets:
  N1: LCD_1602.SCL, T-Cobbler.SCL1
  N2: LCD_1602.SDA, T-Cobbler.SDA1
  N3: LCD_1602.VCC, T-Cobbler.5V0#20
  N4: LCD_1602.GND, T-Cobbler.GND#22
  N5: R1.Pin_0, S1.pin_1, T-Cobbler.GPIO18
  N6: R1.Pin_1, DHT11.VCC, T-Cobbler.3V3#0
  N7: DHT11.SIG, T-Cobbler.GPIO22
  GND: DHT11.GND, S1.pin_2, T-Cobbler.GND#4, RBG.GND
  N8: T-Cobbler.GPIO17, RBG.R
  N9: T-Cobbler.GPIO27, RBG.G

custom parts:
  I2C LCD1602: I2C LCD1602 module of SunFounder Sensor Kit
  DHT11 Humiture Sensor: DHT11 Humiture Sensor module of SunFounder Sensor Kit
  T-Cobbler: T-Cobbler for RPi B+ and Rpi2 from SunFounder
  Dule-Color LED: DuleColor LED module of SunFounder Sensor Kit
