# Fritzing sketch gordonnet_tempmon2 (saved by Fritzing 0.9.3b)
breadboards: 1

parts:
  module5 = I2C LCD1602
  R1 = Resistor [tolerance=±5% resistance=10k package=THT]
  module6 = DHT11 Humiture Sensor
  S1 = Reed switch [package=THT]
  T-Cobbler2 = T-Cobbler
  module7 = Dule-Color LED

nets:
  N1: module5.SCL, T-Cobbler2.SCL1
  N2: module5.SDA, T-Cobbler2.SDA1
  N3: module5.VCC, T-Cobbler2.5V0#20
  N4: module5.GND, T-Cobbler2.GND#22
  N5: R1.Pin_0, S1.pin_1, T-Cobbler2.GPIO18
  N6: R1.Pin_1, module6.VCC, T-Cobbler2.3V3#0
  N7: module6.SIG, T-Cobbler2.GPIO22
  GND: module6.GND, S1.pin_2, T-Cobbler2.GND#4, module7.GND
  N8: T-Cobbler2.GPIO17, module7.R
  N9: T-Cobbler2.GPIO27, module7.G

notes:
  I2C LCD1602

custom parts:
  I2C LCD1602: I2C LCD1602 module of SunFounder Sensor Kit
  DHT11 Humiture Sensor: DHT11 Humiture Sensor module of SunFounder Sensor Kit
  T-Cobbler: T-Cobbler for RPi B+ and Rpi2 from SunFounder
  Dule-Color LED: DuleColor LED module of SunFounder Sensor Kit
